# Fritzing sketch schema (saved by Fritzing 0.9.2b)
breadboards: 1

parts:
  Onderdeel1 = Arduino Uno (Rev3)
  U1 = ESP8266 WiFi Module [part_number=ESP8266]
  BREAKOUT1 = HMC5883L Compass Breakout

nets:
  N1: Onderdeel1.D10_PWM/SS, U1.TXD
  N2: Onderdeel1.D11_PWM/MOSI, U1.RXD
  N3: Onderdeel1.A4/SDA, BREAKOUT1.SDA
  N4: Onderdeel1.A5/SCL, BREAKOUT1.SCL
  3V3: Onderdeel1.3V3, U1.VCC, U1.CH_PD, BREAKOUT1.VIN
  GND: Onderdeel1.GND, U1.GND, BREAKOUT1.GND

custom parts:
  ESP8266 WiFi Module: Generic WiFi Module based on the ESP8266 with onboard PCB antenna and UART communications
